# Fritzing sketch sensor (saved by Fritzing 0.9.3b)

parts:
  Composant1 = Arduino Pro Mini (3.3V)
  DS1 = DS18B20 1-Wire Temperature Sensor [part_number=DS18B20]
  VCC1 = Battery
  Composant2 = NRF24L01+ Breakout Board
  R1 = Resistor [tolerance=±5% resistance=4.7k package=THT]

nets:
  N1: Composant1.RAW, VCC1.+
  GND: Composant1.GND, DS1.GND, VCC1.-, Composant2.GND
  VCC: Composant1.VCC, DS1.VDD, Composant2.VCC, R1.Pin_0
  N2: Composant1.SCK, Composant2.SCK
  N3: Composant1.MISO, Composant2.MISO
  N4: Composant1.MOSI, Composant2.MOSI
  N5: Composant1.D10, Composant2.CS
  N6: Composant1.D9, Composant2.CE
  N7: Composant1.D2, DS1.DQ, R1.Pin_1
